// Digital circuit 16bit_adder.dig as structural Verilog
module _16bit_adder (
  input  in_1,
  input  in_2,
  input  in_3,
  input  in_4,
  input  in_5,
  input  in_6,
  input  in_7,
  input  in_8,
  input  in_9,
  input  in_10,
  input  in_11,
  input  in_12,
  input  in_13,
  input  in_14,
  input  in_15,
  input  in_16,
  input  in_17,
  input  in_18,
  input  in_19,
  input  in_20,
  input  in_21,
  input  in_22,
  input  in_23,
  input  in_24,
  input  in_25,
  input  in_26,
  input  in_27,
  input  in_28,
  input  in_29,
  input  in_30,
  input  in_31,
  input  in_32,
  input  in_33,
  output out_34,
  output out_35,
  output out_36,
  output out_37,
  output out_38,
  output out_39,
  output out_40,
  output out_41,
  output out_42,
  output out_43,
  output out_44,
  output out_45,
  output out_46,
  output out_47,
  output out_48,
  output out_49,
  output out_50
);

  wire _8bit_adder_1_co;

  _8bit_adder _8bit_adder_1 (
    .CI(in_33), .A0(in_1), .A1(in_2), .A2(in_3), .A3(in_4), .A4(in_5), .A5(in_6), .A6(in_7), .A7(in_8),
    .B0(in_17), .B1(in_18), .B2(in_19), .B3(in_20), .B4(in_21), .B5(in_22), .B6(in_23), .B7(in_24),
    .S0(out_34), .S1(out_35), .S2(out_36), .S3(out_37), .S4(out_38), .S5(out_39), .S6(out_40), .S7(out_41),
    .CO(_8bit_adder_1_co));
  _8bit_adder _8bit_adder_2 (
    .CI(_8bit_adder_1_co), .A0(in_9), .A1(in_10), .A2(in_11), .A3(in_12), .A4(in_13), .A5(in_14), .A6(in_15),
    .A7(in_16), .B0(in_25), .B1(in_26), .B2(in_27), .B3(in_28), .B4(in_29), .B5(in_30), .B6(in_31),
    .B7(in_32), .S0(out_42), .S1(out_43), .S2(out_44), .S3(out_45), .S4(out_46), .S5(out_47), .S6(out_48),
    .S7(out_49), .CO(out_50));
endmodule
