// Digital circuit 16x1_ram.dig as structural Verilog
module _16x1_ram (
  input  A0,
  input  A1,
  input  A2,
  input  A3,
  input  DI,
  input  W,
  output DO
);

  wire _1to2_decoder_1_o0, _1to2_decoder_1_o1, _8x1_ram_1_o, _8x1_ram_2_o;

  _1to2_decoder _1to2_decoder_1 (.I(DI), .S(A3), .O0(_1to2_decoder_1_o0), .O1(_1to2_decoder_1_o1));
  _8x1_ram _8x1_ram_1 (.A0(A0), .A1(A1), .A2(A2), .DI(_1to2_decoder_1_o0), .W(W), .O(_8x1_ram_1_o));
  _8x1_ram _8x1_ram_2 (.A0(A0), .A1(A1), .A2(A2), .DI(_1to2_decoder_1_o1), .W(W), .O(_8x1_ram_2_o));
  _2to1_selector _2to1_selector_1 (.D0(_8x1_ram_1_o), .D1(_8x1_ram_2_o), .S(A3), .O(DO));
endmodule
