// Digital circuit 16x2_ram.dig as structural Verilog
module _16x2_ram (
  input  A0,
  input  A1,
  input  A2,
  input  I0,
  input  I1,
  input  W,
  input  A3,
  output O0,
  output O1
);

  _16x1_ram _16x1_ram_1 (.A0(A0), .A1(A1), .A2(A2), .A3(A3), .DI(I0), .W(W), .DO(O0));
  _16x1_ram _16x1_ram_2 (.A0(A0), .A1(A1), .A2(A2), .A3(A3), .DI(I1), .W(W), .DO(O1));
endmodule
