// Digital circuit 1to2_decoder.dig as structural Verilog
module _1to2_decoder (
  input  I,
  input  S,
  output O0,
  output O1
);

  wire not_1_out;

  not not_1 (not_1_out, S);
  and and_1 (O0, I, not_1_out);
  and and_2 (O1, I, S);
endmodule
