// Digital circuit 2to1_selector.dig as structural Verilog
module _2to1_selector (
  input  D0,
  input  D1,
  input  S,
  output O
);

  wire and_1_out, and_2_out, not_1_out;

  not not_1 (not_1_out, S);
  and and_1 (and_1_out, D0, not_1_out);
  and and_2 (and_2_out, D1, S);
  or or_1 (O, and_1_out, and_2_out);
endmodule
