// Digital circuit 8bit_accumulator.dig as structural Verilog
module _8bit_accumulator (
  input  in_9,
  input  in_10,
  input  in_11,
  input  in_12,
  input  in_13,
  input  in_14,
  input  in_15,
  input  in_16,
  input  in_17,
  input  clk,
  output S0,
  output S1,
  output S2,
  output S3,
  output S4,
  output S5,
  output S6,
  output S7
);

  wire _8bit_adder_1_s0, _8bit_adder_1_s1, _8bit_adder_1_s2, _8bit_adder_1_s3, _8bit_adder_1_s4,
       _8bit_adder_1_s5, _8bit_adder_1_s6, _8bit_adder_1_s7;

  _8bit_adder _8bit_adder_1 (
    .CI(in_17), .A0(in_16), .A1(in_15), .A2(in_14), .A3(in_13), .A4(in_12), .A5(in_11), .A6(in_10),
    .A7(in_9), .B0(S0), .B1(S1), .B2(S2), .B3(S3), .B4(S4), .B5(S5), .B6(S6), .B7(S7), .S0(_8bit_adder_1_s0),
    .S1(_8bit_adder_1_s1), .S2(_8bit_adder_1_s2), .S3(_8bit_adder_1_s3), .S4(_8bit_adder_1_s4),
    .S5(_8bit_adder_1_s5), .S6(_8bit_adder_1_s6), .S7(_8bit_adder_1_s7));  // open: CO
  _8bit_latch_et _8bit_latch_et_1 (
    .D0(_8bit_adder_1_s0), .D1(_8bit_adder_1_s1), .D2(_8bit_adder_1_s2), .D3(_8bit_adder_1_s3),
    .D4(_8bit_adder_1_s4), .D5(_8bit_adder_1_s5), .D6(_8bit_adder_1_s6), .D7(_8bit_adder_1_s7), .C(clk),
    .Q0(S0), .Q1(S1), .Q2(S2), .Q3(S3), .Q4(S4), .Q5(S5), .Q6(S6), .Q7(S7));
endmodule
