// Digital circuit 8bit_adder.dig as structural Verilog
module _8bit_adder (
  input  CI,
  input  A0,
  input  A1,
  input  A2,
  input  A3,
  input  A4,
  input  A5,
  input  A6,
  input  A7,
  input  B0,
  input  B1,
  input  B2,
  input  B3,
  input  B4,
  input  B5,
  input  B6,
  input  B7,
  output S0,
  output S1,
  output S2,
  output S3,
  output S4,
  output S5,
  output S6,
  output S7,
  output CO
);

  wire full_adder_1_co, full_adder_2_co, full_adder_3_co, full_adder_4_co, full_adder_5_co, full_adder_6_co,
       full_adder_7_co;

  full_adder full_adder_1 (.CI(CI), .A(A0), .B(B0), .SO(S0), .CO(full_adder_1_co));
  full_adder full_adder_2 (.CI(full_adder_1_co), .A(A1), .B(B1), .SO(S1), .CO(full_adder_2_co));
  full_adder full_adder_3 (.CI(full_adder_2_co), .A(A2), .B(B2), .SO(S2), .CO(full_adder_3_co));
  full_adder full_adder_4 (.CI(full_adder_3_co), .A(A3), .B(B3), .SO(S3), .CO(full_adder_4_co));
  full_adder full_adder_5 (.CI(full_adder_4_co), .A(A4), .B(B4), .SO(S4), .CO(full_adder_5_co));
  full_adder full_adder_6 (.CI(full_adder_5_co), .A(A5), .B(B5), .SO(S5), .CO(full_adder_6_co));
  full_adder full_adder_7 (.CI(full_adder_6_co), .A(A6), .B(B6), .SO(S6), .CO(full_adder_7_co));
  full_adder full_adder_8 (.CI(full_adder_7_co), .A(A7), .B(B7), .SO(S7), .CO(CO));
endmodule
