// Digital circuit 8bit_latch.dig as structural Verilog
module _8bit_latch (
  input  D0,
  input  Clk,
  input  D1,
  input  D2,
  input  D3,
  input  D4,
  input  D5,
  input  D6,
  input  D7,
  output Q0,
  output Q1,
  output Q2,
  output Q3,
  output Q4,
  output Q5,
  output Q6,
  output Q7
);

  // d_flip_flop d_flip_flop_1: pin names not known; wires that end beside it: Clk, D0, Q0
  // d_flip_flop d_flip_flop_2: pin names not known; wires that end beside it: Clk, D1, Q1
  // d_flip_flop d_flip_flop_3: pin names not known; wires that end beside it: Clk, D2, Q2
  // d_flip_flop d_flip_flop_4: pin names not known; wires that end beside it: Clk, D3, Q3
  // d_flip_flop d_flip_flop_5: pin names not known; wires that end beside it: Clk, D4, Q4
  // d_flip_flop d_flip_flop_6: pin names not known; wires that end beside it: Clk, D5, Q5
  // d_flip_flop d_flip_flop_7: pin names not known; wires that end beside it: Clk, D6, Q6
  // d_flip_flop d_flip_flop_8: pin names not known; wires that end beside it: Clk, D7, Q7
endmodule
