// Digital circuit 8bit_latch_clear.dig as structural Verilog
module _8bit_latch_clear (
  input  D0,
  input  D1,
  input  D2,
  input  D3,
  input  D4,
  input  D5,
  input  D6,
  input  D7,
  input  C,
  input  Clr,
  output Q0,
  output Q1,
  output Q2,
  output Q3,
  output Q4,
  output Q5,
  output Q6,
  output Q7
);

  d_flip_flop_clear d_flip_flop_clear_1 (.D(D0), .C(C), .Clr(Clr), .Q(Q0));  // open: nQ
  d_flip_flop_clear d_flip_flop_clear_2 (.D(D1), .C(C), .Clr(Clr), .Q(Q1));  // open: nQ
  d_flip_flop_clear d_flip_flop_clear_3 (.D(D2), .C(C), .Clr(Clr), .Q(Q2));  // open: nQ
  d_flip_flop_clear d_flip_flop_clear_4 (.D(D3), .C(C), .Clr(Clr), .Q(Q3));  // open: nQ
  d_flip_flop_clear d_flip_flop_clear_5 (.D(D4), .C(C), .Clr(Clr), .Q(Q4));  // open: nQ
  d_flip_flop_clear d_flip_flop_clear_6 (.D(D5), .C(C), .Clr(Clr), .Q(Q5));  // open: nQ
  d_flip_flop_clear d_flip_flop_clear_7 (.D(D6), .C(C), .Clr(Clr), .Q(Q6));  // open: nQ
  d_flip_flop_clear d_flip_flop_clear_8 (.D(D7), .C(C), .Clr(Clr), .Q(Q7));  // open: nQ
endmodule
