// Digital circuit 8bit_selector.dig as structural Verilog
module _8bit_selector (
  input  S,
  input  B0,
  input  A0,
  input  B1,
  input  B2,
  input  B3,
  input  B4,
  input  B5,
  input  B6,
  input  B7,
  input  A1,
  input  A2,
  input  A3,
  input  A4,
  input  A5,
  input  A6,
  input  A7,
  output D0,
  output D1,
  output D2,
  output D3,
  output D4,
  output D5,
  output D6,
  output D7
);

  selector selector_1 (.B(B0), .S(S), .A(A0), .O(D0));
  selector selector_2 (.B(B1), .S(S), .A(A1), .O(D1));
  selector selector_3 (.B(B2), .S(S), .A(A2), .O(D2));
  selector selector_4 (.B(B3), .S(S), .A(A3), .O(D3));
  selector selector_5 (.B(B4), .S(S), .A(A4), .O(D4));
  selector selector_6 (.B(B5), .S(S), .A(A5), .O(D5));
  selector selector_7 (.B(B6), .S(S), .A(A6), .O(D6));
  selector selector_8 (.B(B7), .S(S), .A(A7), .O(D7));
endmodule
