// Digital circuit 8x1_ram.dig as structural Verilog
module _8x1_ram (
  input  A0,
  input  A1,
  input  A2,
  input  DI,
  input  W,
  output O
);

  wire _3to8_decoder_1_o0, _3to8_decoder_1_o1, _3to8_decoder_1_o2, _3to8_decoder_1_o3, _3to8_decoder_1_o4,
       _3to8_decoder_1_o5, _3to8_decoder_1_o6, _3to8_decoder_1_o7, d_ff_1_q, d_ff_2_q, d_ff_3_q, d_ff_4_q,
       d_ff_5_q, d_ff_6_q, d_ff_7_q, d_ff_8_q;

  _3to8_decoder _3to8_decoder_1 (
    .D(W), .S0(A0), .S1(A1), .S2(A2), .O0(_3to8_decoder_1_o0), .O1(_3to8_decoder_1_o1),
    .O2(_3to8_decoder_1_o2), .O3(_3to8_decoder_1_o3), .O4(_3to8_decoder_1_o4), .O5(_3to8_decoder_1_o5),
    .O6(_3to8_decoder_1_o6), .O7(_3to8_decoder_1_o7));
  D_FF d_ff_1 (.D(DI), .C(_3to8_decoder_1_o0), .Q(d_ff_1_q));  // open: nQ
  D_FF d_ff_2 (.D(DI), .C(_3to8_decoder_1_o1), .Q(d_ff_2_q));  // open: nQ
  D_FF d_ff_3 (.D(DI), .C(_3to8_decoder_1_o2), .Q(d_ff_3_q));  // open: nQ
  D_FF d_ff_4 (.D(DI), .C(_3to8_decoder_1_o3), .Q(d_ff_4_q));  // open: nQ
  D_FF d_ff_5 (.D(DI), .C(_3to8_decoder_1_o4), .Q(d_ff_5_q));  // open: nQ
  D_FF d_ff_6 (.D(DI), .C(_3to8_decoder_1_o5), .Q(d_ff_6_q));  // open: nQ
  D_FF d_ff_7 (.D(DI), .C(_3to8_decoder_1_o6), .Q(d_ff_7_q));  // open: nQ
  D_FF d_ff_8 (.D(DI), .C(_3to8_decoder_1_o7), .Q(d_ff_8_q));  // open: nQ
  _8to1_selector _8to1_selector_1 (
    .D0(d_ff_1_q), .D1(d_ff_2_q), .D2(d_ff_3_q), .D3(d_ff_4_q), .D4(d_ff_5_q), .D5(d_ff_6_q), .D6(d_ff_7_q),
    .D7(d_ff_8_q), .S0(A0), .S1(A1), .S2(A2), .O(O));
endmodule
