// Digital circuit 8x2_ram.dig as structural Verilog
module _8x2_ram (
  input  A0,
  input  A1,
  input  A2,
  input  I0,
  input  I1,
  input  W,
  output O1,
  output O0
);

  _8x1_ram _8x1_ram_1 (.A0(A0), .A1(A1), .A2(A2), .DI(I0), .W(W), .O(O0));
  _8x1_ram _8x1_ram_2 (.A0(A0), .A1(A1), .A2(A2), .DI(I1), .W(W), .O(O1));
endmodule
