// Digital circuit add_sub.dig as structural Verilog
module add_sub (
  input  A0,
  input  A1,
  input  A2,
  input  A3,
  input  A4,
  input  A5,
  input  A6,
  input  A7,
  input  B0,
  input  B1,
  input  B2,
  input  B3,
  input  B4,
  input  B5,
  input  B6,
  input  B7,
  input  SUB,
  output S0,
  output S1,
  output S2,
  output S3,
  output S4,
  output S5,
  output S6,
  output S7,
  output OF
);

  wire _8bit_adder_1_co, inverter_1_o0, inverter_1_o1, inverter_1_o2, inverter_1_o3, inverter_1_o4,
       inverter_1_o5, inverter_1_o6, inverter_1_o7;

  inverter inverter_1 (
    .I0(B0), .I1(B1), .I2(B2), .I3(B3), .I4(B4), .I5(B5), .I6(B6), .I7(B7), .Invert(SUB), .O0(inverter_1_o0),
    .O1(inverter_1_o1), .O2(inverter_1_o2), .O3(inverter_1_o3), .O4(inverter_1_o4), .O5(inverter_1_o5),
    .O6(inverter_1_o6), .O7(inverter_1_o7));
  _8bit_adder _8bit_adder_1 (
    .CI(SUB), .A0(A0), .A1(A1), .A2(A2), .A3(A3), .A4(A4), .A5(A5), .A6(A6), .A7(A7), .B0(inverter_1_o0),
    .B1(inverter_1_o1), .B2(inverter_1_o2), .B3(inverter_1_o3), .B4(inverter_1_o4), .B5(inverter_1_o5),
    .B6(inverter_1_o6), .B7(inverter_1_o7), .S0(S0), .S1(S1), .S2(S2), .S3(S3), .S4(S4), .S5(S5), .S6(S6),
    .S7(S7), .CO(_8bit_adder_1_co));
  xor xor_1 (OF, _8bit_adder_1_co, SUB);
endmodule
