// Digital circuit d_flip_flop.dig as structural Verilog
module d_flip_flop (
  input  H,
  input  D,
  output Q,
  output nQ
);

  wire and_1_out, and_2_out, not_1_out;

  not not_1 (not_1_out, D);
  and and_1 (and_1_out, not_1_out, H);
  and and_2 (and_2_out, H, D);
  rs_flip_flop rs_flip_flop_1 (.R(and_1_out), .S(and_2_out), .Q(Q), .nQ(nQ));
endmodule
