// Digital circuit d_flip_flop_clear.dig as structural Verilog
module d_flip_flop_clear (
  input  D,
  input  C,
  input  Clr,
  output Q,
  output nQ
);

  wire and_1_out, and_2_out, not_1_out, or_1_out;

  not not_1 (not_1_out, D);
  and and_1 (and_1_out, not_1_out, C);
  and and_2 (and_2_out, C, D);
  or or_1 (or_1_out, Clr, and_1_out);
  rs_flip_flop rs_flip_flop_1 (.R(or_1_out), .S(and_2_out), .Q(Q), .nQ(nQ));
endmodule
