// Digital circuit d_flip_flop_et.dig as structural Verilog
module d_flip_flop_et (
  input  D,
  input  C,
  output Q,
  output nQ
);

  wire and_1_out, and_2_out, and_3_out, and_4_out, not_1_out, not_2_out, rs_ff_as_1_nq, rs_ff_as_1_q;

  not not_1 (not_1_out, C);
  not not_2 (not_2_out, D);
  and and_1 (and_1_out, D, not_1_out);
  and and_2 (and_2_out, not_1_out, not_2_out);
  RS_FF_AS rs_ff_as_1 (.S(and_2_out), .R(and_1_out), .Q(rs_ff_as_1_q), .nQ(rs_ff_as_1_nq));
  and and_3 (and_3_out, rs_ff_as_1_q, C);
  and and_4 (and_4_out, C, rs_ff_as_1_nq);
  RS_FF_AS rs_ff_as_2 (.S(and_4_out), .R(and_3_out), .Q(Q), .nQ(nQ));
endmodule
