// Digital circuit full_adder.dig as structural Verilog
module full_adder (
  input  CI,
  input  A,
  input  B,
  output SO,
  output CO
);

  wire half_adder_1_co, half_adder_1_so, half_adder_2_co;

  half_adder half_adder_1 (.A(A), .B(B), .SO(half_adder_1_so), .CO(half_adder_1_co));
  half_adder half_adder_2 (.A(CI), .B(half_adder_1_so), .SO(SO), .CO(half_adder_2_co));
  or or_1 (CO, half_adder_2_co, half_adder_1_co);
endmodule
