// Digital circuit inverter.dig as structural Verilog
module inverter (
  input  I0,
  input  I1,
  input  I2,
  input  I3,
  input  I4,
  input  I5,
  input  I6,
  input  I7,
  input  Invert,
  output O0,
  output O1,
  output O2,
  output O3,
  output O4,
  output O5,
  output O6,
  output O7
);

  xor xor_1 (O0, I0, Invert);
  xor xor_2 (O1, I1, Invert);
  xor xor_3 (O2, I2, Invert);
  xor xor_4 (O3, I3, Invert);
  xor xor_5 (O4, I4, Invert);
  xor xor_6 (O5, I5, Invert);
  xor xor_7 (O6, I6, Invert);
  xor xor_8 (O7, I7, Invert);
endmodule
