// Digital circuit oscillator.dig as structural Verilog
module oscillator (
  output out_1
);

  wire switch_1_b;

  Switch switch_1 (.A(out_1), .B(switch_1_b));
  not not_1 (out_1, switch_1_b);
endmodule
