// Digital circuit rs_flip_flop.dig as structural Verilog
module rs_flip_flop (
  input  R,
  input  S,
  output Q,
  output nQ
);

  nor nor_1 (Q, R, nQ);
  nor nor_2 (nQ, Q, S);

  // Notes on the sheet:
  //   R: default 1
endmodule
