// Digital circuit selector.dig as structural Verilog
module selector (
  input  B,
  input  S,
  input  A,
  output O
);

  wire and_1_out, and_2_out, not_1_out;

  not not_1 (not_1_out, S);
  and and_1 (and_1_out, B, S);
  and and_2 (and_2_out, A, not_1_out);
  or or_1 (O, and_1_out, and_2_out);
endmodule
