// Digital circuit test.dig as structural Verilog
module test (
  input  clk,
  input  in_2,
  output out_3,
  output out_4
);

  // d_flip_flop d_flip_flop_1: pin names not known; wires that end beside it: clk, in_2, out_3, out_4
endmodule
