// Digital circuit cat2.dig as structural Verilog
module cat2 (
  input  in_2,
  input  in_3,
  input  in_4,
  input  in_5,
  output out_1
);

  wire and_1_out, and_2_out, and_3_out, color_1_b, color_1_t, color_1_w, neutered_1_n, not_1_out, or_1_out,
       or_2_out, sexual_1_f, sexual_1_m;

  sexual sexual_1 (.Ss(in_2), .F(sexual_1_f), .M(sexual_1_m));
  neutered neutered_1 (.Ns(in_3), .N(neutered_1_n));  // open: U
  color color_1 (.C1(in_4), .C2(in_5), .W(color_1_w), .B(color_1_b), .T(color_1_t));  // open: O
  not not_1 (not_1_out, color_1_w);
  or or_1 (or_1_out, color_1_w, color_1_t);
  and and_1 (and_1_out, sexual_1_f, not_1_out);
  and and_2 (and_2_out, sexual_1_m, or_1_out);
  or or_2 (or_2_out, and_1_out, and_2_out);
  and and_3 (and_3_out, or_2_out, neutered_1_n);
  or or_3 (out_1, and_3_out, color_1_b);
endmodule
