// Digital circuit cat_panel.dig as structural Verilog
module cat_panel (
  input  C1,
  input  C2,
  input  Ss,
  input  Ns,
  output W,
  output B,
  output T,
  output O,
  output F,
  output M,
  output N,
  output U
);

  wire not_3_out, not_4_out;

  not not_1 (M, Ss);
  not not_2 (U, Ns);
  not not_3 (not_3_out, C1);
  not not_4 (not_4_out, C2);
  and and_1 (W, not_3_out, not_4_out);
  and and_2 (B, C1, not_4_out);
  and and_3 (T, not_3_out, C2);
  and and_4 (O, C1, C2);

  assign F = Ss;
  assign N = Ns;
endmodule
