// Digital circuit color.dig as structural Verilog
module color (
  input  C1,
  input  C2,
  output W,
  output B,
  output T,
  output O
);

  wire not_1_out, not_2_out;

  not not_1 (not_1_out, C1);
  not not_2 (not_2_out, C2);
  and and_1 (W, not_1_out, not_2_out);
  and and_2 (B, C1, not_2_out);
  and and_3 (T, not_1_out, C2);
  and and_4 (O, C1, C2);
endmodule
